// Logisim project BAI1.1.circ as structural Verilog: 1 circuit, main circuit main
module main (
  input  A,
  input  B,
  output A_prime,
  output AND,
  output OR,
  output NAND,
  output NOR,
  output XOR,
  output NXOR
);

  not not_1 (A_prime, A);
  and and_1 (AND, A, B);
  or or_1 (OR, A, B);
  nand nand_1 (NAND, A, B);
  nor nor_1 (NOR, A, B);
  xor xor_1 (XOR, A, B);
  xnor xnor_1 (NXOR, A, B);
endmodule
