// Logisim project tn1.circ as structural Verilog: 1 circuit, main circuit main
module main (
  input  A,
  input  B,
  input  C,
  output A_prime,
  output AND,
  output OR,
  output NOR,
  output CHAIN,
  output XOR,
  output NXOR,
  output XOR3,
  output NAND_3
);

  wire nand_1_out;

  not not_1 (A_prime, A);
  and and_1 (AND, A, B);
  or or_1 (OR, A, B);
  nand nand_1 (nand_1_out, A, B);
  nor nor_1 (NOR, A, B);
  xor xor_1 (XOR, A, B);
  xnor xnor_1 (NXOR, A, B);
  ExactlyOne xor_2 (.out(XOR3), .in0(A), .in2(B), .in4(C));
  nand nand_2 (NAND_3, A, B, C);
  nand u_nand_3 (CHAIN, nand_1_out, C);
endmodule
