// Logisim project warmup.circ as structural Verilog: 1 circuit, main circuit main
module main (
  input  A,
  input  F,
  input  B
);

  wire and_1_out, not_1_out;

  not not_1 (not_1_out, B);
  and and_1 (and_1_out, A, not_1_out);
endmodule
